# Fritzing sketch atlas_shield (saved by Fritzing 0.7.12b)
breadboards: 1

parts:
  Arduino1 = Arduino
  MUX = IC, DIP package, 16 pins [chip_label=74HC4052]
  J1 = female pin header, 3 pins [form="♀ (female)"]
  J2 = female pin header, 3 pins [form="♀ (female)"]
  J3 = female pin header, 3 pins [form="♀ (female)"]
  J4 = female pin header, 3 pins [form="♀ (female)"]
  J5 = female pin header, 3 pins [form="♀ (female)"]
  J6 = female pin header, 3 pins [form="♀ (female)"]
  J7 = female pin header, 3 pins [form="♀ (female)"]
  J8 = female pin header, 3 pins [form="♀ (female)"]
  J9 = Screw terminal - 2 pins [package=THT]
  J10 = Screw terminal - 2 pins [package=THT]
  J11 = Screw terminal - 2 pins [package=THT]
  J12 = Screw terminal - 2 pins [package=THT]

nets:
  N1: Arduino1.GND, MUX.pin6, MUX.pin7, MUX.pin8, J1.pin3, J3.pin3, J5.pin3, J7.pin3
  N2: Arduino1.D9, MUX.pin13
  N3: Arduino1.D8, MUX.pin3
  N4: Arduino1.D3, MUX.pin9
  N5: Arduino1.D2, MUX.pin10
  N6: Arduino1.3V3, MUX.pin16, J2.pin3, J4.pin3, J6.pin3, J8.pin3
  N7: MUX.pin1, J1.pin2
  N8: MUX.pin2, J5.pin2
  N9: MUX.pin4, J7.pin2
  N10: MUX.pin5, J3.pin2
  N11: MUX.pin11, J7.pin1
  N12: MUX.pin12, J1.pin1
  N13: MUX.pin14, J3.pin1
  N14: MUX.pin15, J5.pin1
  N15: J2.pin1, J9.pin1
  N16: J2.pin2, J9.pin2
  N17: J4.pin1, J10.pin1
  N18: J4.pin2, J10.pin2
  N19: J6.pin1, J11.pin1
  N20: J6.pin2, J11.pin2
  N21: J8.pin1, J12.pin1
  N22: J8.pin2, J12.pin2

notes:
  1Y3
  1Y2
  1Y1
  1Y0
  2Y3
  2Y2
  2Y1
  2Y0
  S0
  S1
  2Z
  1Z
  Circuit 0
  Circuit 1
  Circuit 2
  Circuit 3
  CC-BY Russell Neches
  Atlas Shield
  v1
  d2=1
  d2=0
  d3=1
  d3=0
  3
  2
  1
  0
